// Logisim project TN1.circ as structural Verilog: 3 circuits, main circuit main
module main (
  input  X,
  input  Y,
  input  Z,
  output f
);

  and and_1 (f, X, Y, Z);
endmodule

module Warmup (
  input  A,
  input  B,
  output F
);

  wire not_1_out;

  not not_1 (not_1_out, B);
  and and_1 (F, A, not_1_out);
endmodule

module TN1 (
  input  A,
  input  B,
  input  C,
  output A_prime,
  output E,
  output F,
  output G,
  output H,
  output I,
  output J,
  output XOR3,
  output CHAIN,
  output NAND3
);

  wire nand_1_out;

  not not_1 (A_prime, A);
  nand nand_1 (nand_1_out, A, B);
  nand nand_2 (NAND3, A, B, C);
  and AND (E, A, B);
  or OR (F, A, B);
  nand NAND_3 (G, A, B);
  nor NOR (H, A, B);
  xor XOR (I, A, B);
  xnor XNOR (J, A, B);
  ExactlyOne xor_2 (.out(XOR3), .in0(A), .in1(B), .in2(C));
  nand nand_4 (CHAIN, nand_1_out, C);
endmodule
